// Logisim project Control Unit.circ as structural Verilog
// Chrono
module Control_Unit_2 (
  input  Start,
  input  Fetched,
  input  Halt_Instruction,
  input  Ejecutada,
  input  in_5,
  input  in_6,
  input  [3:0] in_7,
  input  in_8,
  input  in_9,
  input  in_10,
  input  [3:0] in_11,
  output out_12,
  output CS,
  output out_14,
  output out_15,
  output out_16,
  output out_17
);

  wire Chrono1_Reset, Chrono2_Reset, chronometer_1_finish, CS_t, d_ff_1_q, d_ff_5_q, demultiplexer_2_out0,
       demultiplexer_2_out1, demultiplexer_3_out0, demultiplexer_4_out0, demultiplexer_5_out0,
       demultiplexer_5_out1, demultiplexer_6_out0, demultiplexer_7_out0, demultiplexer_7_out1,
       demultiplexer_8_out0, demultiplexer_8_out1, Enable_PC, Execute, Execute_Finished, Execute_In_Progress,
       Fecth_Finished, Fetch, Fetched_t, Halt_State, or_3_out, or_7_out, or_9_out, or_12_out, PC_Address,
       R_W_Done, R_W_RAM, RAM, undriven, undriven_2;
  wire [3:0] multiplexer_1_out;

  Demultiplexer #(.enable("false")) demultiplexer_1 (
    .out0(Execute_Finished), .out1(Chrono2_Reset), .in(Execute_In_Progress), .sel(RAM));
  Multiplexer #(.width(4), .enable("false")) multiplexer_1 (
    .in0(in_7), .in1(in_11), .out(multiplexer_1_out), .sel(in_10));
  Demultiplexer #(.enable("false")) demultiplexer_2 (
    .out0(demultiplexer_2_out0), .out1(demultiplexer_2_out1), .in(demultiplexer_2_out0), .sel(Start));
  or or_1 (Enable_PC, R_W_Done, Execute_Finished);
  or or_2 (CS_t, Fetch, Execute);
  Demultiplexer #(.enable("false")) demultiplexer_3 (
    .out0(demultiplexer_3_out0), .out1(Chrono1_Reset), .in(d_ff_1_q), .sel(in_9));
  D_Flip_Flop d_ff_1 (.clk(in_5), .D(demultiplexer_3_out0), .Q(d_ff_1_q), .preset(in_9));  // open: Qn, en, reset
  or or_3 (or_3_out, demultiplexer_4_out0, Chrono2_Reset);
  Chronometer chronometer_1 (
    .in_1(multiplexer_1_out), .in_2(Chrono2_Reset), .in_3(in_5), .Finish(chronometer_1_finish));
  or or_4 (out_12, demultiplexer_5_out0, demultiplexer_8_out1, demultiplexer_2_out1);
  D_Flip_Flop d_ff_2 (.clk(in_5), .D(or_3_out), .Q(Execute), .reset(in_9));  // open: Qn, preset, en
  or or_5 (R_W_RAM, in_10, Execute);
  or or_6 (PC_Address, Fetch, Chrono1_Reset, Enable_PC);
  Demultiplexer #(.enable("false")) demultiplexer_4 (
    .out0(demultiplexer_4_out0), .out1(out_16), .in(Execute), .sel(chronometer_1_finish));
  or or_7 (or_7_out, demultiplexer_6_out0, or_9_out, Chrono1_Reset);
  or or_8 (RAM, in_10, in_6);
  Demultiplexer #(.enable("false")) demultiplexer_5 (
    .out0(demultiplexer_5_out0), .out1(demultiplexer_5_out1), .in(out_12));  // open: sel
  D_Flip_Flop d_ff_3 (.clk(in_5), .D(or_7_out), .Q(Fetch), .reset(in_9));  // open: Qn, preset, en
  D_Flip_Flop d_ff_4 (.clk(in_5), .D(out_16), .Q(R_W_Done), .reset(in_9));  // open: Qn, preset, en
  or or_9 (or_9_out, Execute_Finished, R_W_Done);
  Demultiplexer #(.enable("false")) demultiplexer_6 (
    .out0(demultiplexer_6_out0), .out1(Fecth_Finished), .in(Fetch), .sel(Fetched_t));
  Demultiplexer #(.enable("false")) demultiplexer_7 (
    .out0(demultiplexer_7_out0), .out1(demultiplexer_7_out1), .in(demultiplexer_5_out1),
    .sel(Halt_Instruction));
  or or_10 (out_14, demultiplexer_8_out0, demultiplexer_7_out0);
  Chronometer chronometer_2 (.in_1(in_7), .in_2(Chrono1_Reset), .in_3(in_5), .Finish(Fetched_t));
  Demultiplexer demultiplexer_8 (
    .out0(demultiplexer_8_out0), .out1(demultiplexer_8_out1), .in(out_14), .en(Ejecutada));  // open: sel
  D_Flip_Flop d_ff_5 (.clk(in_5), .D(Fecth_Finished), .Q(d_ff_5_q), .reset(in_9));  // open: Qn, preset, en
  Demultiplexer #(.enable("false")) demultiplexer_9 (
    .out0(Execute_In_Progress), .out1(Halt_State), .in(d_ff_5_q), .sel(in_8));
  or or_11 (CS, undriven, undriven_2);
  or or_12 (or_12_out, out_15, Halt_State);
  D_Flip_Flop d_ff_6 (.clk(in_5), .D(or_12_out), .Q(out_15), .reset(in_9));  // open: Qn, preset, en

  // Other names for the same wires on the sheet: Clock = in_5; Enable_Instruction = out_17; End = out_15; Halt = in_8;
  //   Idle_Finished = Chrono1_Reset; R_W_Execution = Chrono2_Reset; Read_End = out_16; Read_RAM = in_6;
  //   Read_Time[3:0] = in_7; Reset = in_9; Write_RAM = in_10; Write_Time[3:0] = in_11

  // Notes on the sheet:
  //   Iddle
  //   Inputs
  //   Outputs
  //   Idle
  //   Execution Progress
  //   Capturar Instruccion
  //   Fetch
  //   Esquema de guia
  //   Execute
  //   Fetch Progress
  //   Execute
  //   Captura Instruccion
  //   Ejecuta Instruccion 
  //   End
  //   End
endmodule

module Chronometer (
  input  [3:0] in_1,
  input  in_2,
  input  in_3,
  output Finish
);

  wire [3:0] counter_1_q;

  Counter #(.width(4), .max('hf)) counter_1 (
    .count(1'b1), .Q(counter_1_q), .clk(in_3), .clr(in_2));  // open: load, D, carry
  Comparator #(.width(4)) comparator_1 (.a(in_1), .b(counter_1_q), .eq(Finish));  // open: gt, lt

  // Other names for the same wires on the sheet: Clock = in_3; Reset = in_2; Time[3:0] = in_1

  // Notes on the sheet:
  //   Inputs
  //   Output
endmodule
