// Logisim project Para_Trabajar.circ as structural Verilog
module Program_Counter_2 (
  input  [31:0] Branch_Control,
  input  Reset,
  input  Enabled,
  input  Clock,
  output [31:0] Instruction
);

  Register #(.width(32)) PC (.D(Branch_Control), .en(Enabled), .Q(Instruction), .clk(Clock), .clr(Reset));
endmodule

module Register_File (
  input  [4:0] DA,
  input  [31:0] DI,
  input  R_W,
  input  [4:0] SA,
  input  [4:0] SB,
  input  Clk,
  input  Reset,
  output [31:0] A,
  output [31:0] B
);

  wire L0, L1, L2, L3, L4, L5, L6, L7, L8, L9, L10, L11, L12, L13, L14, L15, L16, L17, L18, L19, L20, L21,
       L22, L23, L24, L25, L26, L27, L28, L29, L30, L31;
  wire [31:0] Q0, Q1, Q2, Q3, Q4, Q5, Q6, Q7, Q8, Q9, Q10, Q11, Q12, Q13, Q14, Q16, Q17, Q18, Q19, Q20, Q21,
       Q22, Q23, Q24, Q25, Q26, Q27, Q28, Q29, Q30, Q31;

  Decoder #(.select(5), .disabled(0)) decoder_1 (
    .out0(L0), .out1(L1), .out2(L2), .out3(L3), .out4(L4), .out5(L5), .out6(L6), .out7(L7), .out8(L8),
    .out9(L9), .out10(L10), .out11(L11), .out12(L12), .out13(L13), .out14(L14), .out15(L15), .out16(L16),
    .out17(L17), .out18(L18), .out19(L19), .out20(L20), .out21(L21), .out22(L22), .out23(L23), .out24(L24),
    .out25(L25), .out26(L26), .out27(L27), .out28(L28), .out29(L29), .out30(L30), .out31(L31), .sel(DA),
    .en(R_W));
  Register #(.width(32)) R00 (.D(DI), .en(L0), .Q(Q0), .clk(Clk), .clr(Reset));
  Register #(.width(32)) R04 (.D(DI), .en(L4), .Q(Q4), .clk(Clk), .clr(Reset));
  Register #(.width(32)) R08 (.D(DI), .en(L8), .Q(Q8), .clk(Clk), .clr(Reset));
  Register #(.width(32)) R12 (.D(DI), .en(L12), .Q(Q12), .clk(Clk), .clr(Reset));
  Register #(.width(32)) R16 (.D(DI), .en(L16), .Q(Q16), .clk(Clk), .clr(Reset));
  Register #(.width(32)) R20 (.D(DI), .en(L20), .Q(Q20), .clk(Clk), .clr(Reset));
  Register #(.width(32)) R24 (.D(DI), .en(L24), .Q(Q24), .clk(Clk), .clr(Reset));
  Register #(.width(32)) R28 (.D(DI), .en(L28), .Q(Q28), .clk(Clk), .clr(Reset));
  Register #(.width(32)) R01 (.D(DI), .en(L1), .Q(Q1), .clk(Clk), .clr(Reset));
  Register #(.width(32)) R05 (.D(DI), .en(L5), .Q(Q5), .clk(Clk), .clr(Reset));
  Register #(.width(32)) R09 (.D(DI), .en(L9), .Q(Q9), .clk(Clk), .clr(Reset));
  Register #(.width(32)) R13 (.D(DI), .en(L13), .Q(Q13), .clk(Clk), .clr(Reset));
  Register #(.width(32)) R17 (.D(DI), .en(L17), .Q(Q17), .clk(Clk), .clr(Reset));
  Register #(.width(32)) R21 (.D(DI), .en(L21), .Q(Q21), .clk(Clk), .clr(Reset));
  Register #(.width(32)) R25 (.D(DI), .en(L25), .Q(Q25), .clk(Clk), .clr(Reset));
  Register #(.width(32)) R29 (.D(DI), .en(L29), .Q(Q29), .clk(Clk), .clr(Reset));
  Register #(.width(32)) R02 (.D(DI), .en(L2), .Q(Q2), .clk(Clk), .clr(Reset));
  Register #(.width(32)) R06 (.D(DI), .en(L6), .Q(Q6), .clk(Clk), .clr(Reset));
  Register #(.width(32)) R10 (.D(DI), .en(L10), .Q(Q10), .clk(Clk), .clr(Reset));
  Register #(.width(32)) R14 (.D(DI), .en(L14), .Q(Q14), .clk(Clk), .clr(Reset));
  Register #(.width(32)) R18 (.D(DI), .en(L18), .Q(Q18), .clk(Clk), .clr(Reset));
  Register #(.width(32)) R22 (.D(DI), .en(L22), .Q(Q22), .clk(Clk), .clr(Reset));
  Register #(.width(32)) R26 (.D(DI), .en(L26), .Q(Q26), .clk(Clk), .clr(Reset));
  Register #(.width(32)) R30 (.D(DI), .en(L30), .Q(Q30), .clk(Clk), .clr(Reset));
  Register #(.width(32)) R03 (.D(DI), .en(L3), .Q(Q3), .clk(Clk), .clr(Reset));
  Register #(.width(32)) R07 (.D(DI), .en(L7), .Q(Q7), .clk(Clk), .clr(Reset));
  Register #(.width(32)) R11 (.D(DI), .en(L11), .Q(Q11), .clk(Clk), .clr(Reset));
  Register #(.width(32)) R15 (.D(DI), .en(L15), .Q(Q14), .clk(Clk), .clr(Reset));
  Register #(.width(32)) R19 (.D(DI), .en(L19), .Q(Q19), .clk(Clk), .clr(Reset));
  Register #(.width(32)) R23 (.D(DI), .en(L23), .Q(Q23), .clk(Clk), .clr(Reset));
  Register #(.width(32)) R27 (.D(DI), .en(L27), .Q(Q27), .clk(Clk), .clr(Reset));
  Register #(.width(32)) R31 (.D(DI), .en(L31), .Q(Q31), .clk(Clk), .clr(Reset));
  Multiplexer #(.select(5), .width(32)) multiplexer_1 (
    .in0(Q0), .in1(Q1), .in2(Q2), .in3(Q3), .in4(Q4), .in5(Q5), .in6(Q6), .in7(Q7), .in8(Q8), .in9(Q9),
    .in10(Q10), .in11(Q11), .in12(Q11), .in13(Q13), .in14(Q14), .in15(Q14), .in16(Q16), .in17(Q17),
    .in18(Q18), .in19(Q19), .in20(Q20), .in21(Q21), .in22(Q22), .in23(Q23), .in24(Q24), .in25(Q25),
    .in26(Q26), .in27(Q27), .in28(Q28), .in29(Q29), .in30(Q30), .in31(Q31), .out(A), .sel(SA));  // open: en
  Multiplexer #(.select(5), .width(32)) multiplexer_2 (
    .in0(Q0), .in1(Q1), .in2(Q2), .in3(Q3), .in4(Q4), .in5(Q5), .in6(Q6), .in7(Q7), .in8(Q8), .in9(Q9),
    .in10(Q10), .in11(Q11), .in12(Q11), .in13(Q13), .in14(Q14), .in15(Q14), .in16(Q16), .in17(Q17),
    .in18(Q18), .in19(Q19), .in20(Q20), .in21(Q21), .in22(Q22), .in23(Q23), .in24(Q24), .in25(Q25),
    .in26(Q26), .in27(Q27), .in28(Q28), .in29(Q29), .in30(Q30), .in31(Q31), .out(B), .sel(SB));  // open: en

  // Other names for the same wires on the sheet: D[31:0] = DI; Q15[31:0] = Q14; RES = Reset; RW = R_W

  // Notes on the sheet:
  //   Inputs
  //   Data Address
  //   Data In
  //   Read/Write
  //   Selector A
  //   Selector B
  //   Outputs
  //   Data A
  //   Data B
endmodule

module ALU (
  input  [31:0] A,
  input  [31:0] B,
  input  [3:0] S,
  output [31:0] R,
  output Zero,
  output Neg
);
endmodule

module Sign_Extend (
  input  [15:0] _16_Bit_Input,
  output [31:0] _32_Bit_Output
);

  Multiplexer #(.width(17)) multiplexer_1 (
    .in0({17{1'b0}}), .in1({17{1'b1}}), .out(_32_Bit_Output[31:15]), .sel(_16_Bit_Input[15]));  // open: en

  assign _32_Bit_Output[14:0] = _16_Bit_Input[14:0];
endmodule
