// Logisim project Read_RAM.circ as structural Verilog: 1 circuit, main circuit Read _RAM
module Read__RAM (
  input  [31:0] Dir_RAM,
  input  [31:0] Bank_0,
  input  [31:0] Bank_1,
  input  [31:0] Bank_2,
  input  [31:0] Bank_3,
  output [31:0] Value
);

  wire [1:0] Selector;

  Multiplexer #(.select(2), .width(32), .enable("false")) multiplexer_1 (
    .in0(Bank_0), .in1(Bank_1), .in2(Bank_2), .in3(Bank_3), .out(Value), .sel(Selector));

  // Other names for the same wires on the sheet: Selector_t[1:0] = Dir_RAM[3:2]

  // Notes on the sheet:
  //   Conversion from Little Endian to Big Endian
endmodule
